// Logisim project Logisim01.circ as structural Verilog: 4 circuits, main circuit FirstTask
module FirstTask (
  input  x0,
  input  x1,
  input  x2,
  input  x3,
  output y
);

  wire v3_out, v6_out, v9_out;

  and v3 (v3_out, x0, x1, ~x2, ~x3);  // AND_Gate
  and v6 (v6_out, ~x0, x1, x2, ~x3);  // AND_Gate
  and v9 (v9_out, x0, ~x1, ~x2, x3);  // AND_Gate
  or or_1 (y, v3_out, v6_out, v9_out);

  // Notes on the sheet:
  //   4-bit inpit y=sum (3,6,9)
  //   y=[0011, 0110, 1001]
endmodule

module Main (
);

  wire dipswitch_1_sw1, dipswitch_1_sw2, dipswitch_1_sw3, dipswitch_1_sw4, dipswitch_2_sw1, dipswitch_2_sw2,
       dipswitch_2_sw3, dipswitch_2_sw4, dipswitch_3_sw1, dipswitch_3_sw2, dipswitch_3_sw3, dipswitch_3_sw4,
       firsttask_1_y, secondtask_1_y, thirdtask_1_y;

  DipSwitch #(.number(4)) dipswitch_1 (
    .sw1(dipswitch_1_sw1), .sw2(dipswitch_1_sw2), .sw3(dipswitch_1_sw3), .sw4(dipswitch_1_sw4));
  DipSwitch #(.number(4)) dipswitch_2 (
    .sw1(dipswitch_2_sw1), .sw2(dipswitch_2_sw2), .sw3(dipswitch_2_sw3), .sw4(dipswitch_2_sw4));
  DipSwitch #(.number(4)) dipswitch_3 (
    .sw1(dipswitch_3_sw1), .sw2(dipswitch_3_sw2), .sw3(dipswitch_3_sw3), .sw4(dipswitch_3_sw4));
  FirstTask firsttask_1 (
    .x0(dipswitch_1_sw1), .x1(dipswitch_1_sw2), .x2(dipswitch_1_sw3), .x3(dipswitch_1_sw4), .y(firsttask_1_y));
  LED led_1 (.in(firsttask_1_y));
  SecondTask secondtask_1 (
    .x0(dipswitch_2_sw1), .x1(dipswitch_2_sw2), .x2(dipswitch_2_sw3), .x3(dipswitch_2_sw4), .y(secondtask_1_y));
  LED led_2 (.in(secondtask_1_y));
  ThirdTask thirdtask_1 (
    .x0(dipswitch_3_sw1), .x1(dipswitch_3_sw2), .x2(dipswitch_3_sw3), .x3(dipswitch_3_sw4), .y(thirdtask_1_y));
  LED led_3 (.in(thirdtask_1_y));
endmodule

module SecondTask (
  input  x0,
  input  x1,
  input  x2,
  input  x3,
  output y
);

  wire v1_out, v2_out, v4_out, v6_out, v7_out;

  and v2 (v2_out, ~x0, x1, ~x2, ~x3);  // AND_Gate
  and v7 (v7_out, x0, x1, x2, ~x3);  // AND_Gate
  and v6 (v6_out, ~x0, x1, x2, ~x3);  // AND_Gate
  and v1 (v1_out, x0, ~x1, ~x2, ~x3);  // AND_Gate
  and v4 (v4_out, ~x0, ~x1, x2, ~x3);  // AND_Gate
  or or_1 (y, v2_out, v7_out, v6_out, v1_out, v4_out);

  // Notes on the sheet:
  //   y=[0010, 0111, 0110, 0001, 0100]
  //   y=sum (2,7,6,1,4)
endmodule

module ThirdTask (
  input  x0,
  input  x1,
  input  x2,
  input  x3,
  output y
);

  wire nand_1_out, nand_2_out, nand_3_out, nand_4_out, nand_5_out, nand_6_out, nand_7_out, nand_8_out,
       nand_9_out, nand_10_out, nand_11_out, nand_12_out, nand_13_out, nand_14_out, nand_15_out;

  nand nand_1 (nand_1_out, ~x0, x1, ~x2, ~x3);  // NAND_Gate
  nand nand_2 (nand_2_out, x0, x1, x2, ~x3);  // NAND_Gate
  nand nand_3 (nand_3_out, ~x0, x1, x2, ~x3);  // NAND_Gate
  nand nand_4 (nand_4_out, x0, ~x1, ~x2, ~x3);  // NAND_Gate
  nand nand_5 (nand_5_out, ~x0, ~x1, x2, ~x3);  // NAND_Gate
  nand nand_6 (nand_6_out, nand_1_out, nand_1_out);
  nand nand_7 (nand_7_out, nand_2_out, nand_2_out);
  nand nand_8 (nand_8_out, nand_3_out, nand_3_out);
  nand nand_9 (nand_9_out, nand_4_out, nand_4_out);
  nand nand_10 (nand_10_out, nand_5_out, nand_5_out);
  nand nand_11 (nand_11_out, nand_6_out, nand_6_out);
  nand nand_12 (nand_12_out, nand_7_out, nand_7_out);
  nand nand_13 (nand_13_out, nand_8_out, nand_8_out);
  nand nand_14 (nand_14_out, nand_9_out, nand_9_out);
  nand nand_15 (nand_15_out, nand_10_out, nand_10_out);
  nand nand_16 (y, nand_11_out, nand_12_out, nand_13_out, nand_14_out, nand_15_out);

  // Notes on the sheet:
  //   y=sum (2,7,6,1,4)
  //   y=[0010, 0111, 0110, 0001, 0100]
endmodule
