// Logisim project Logisim2.circ as structural Verilog
module TaskOne (
  input  x0,
  input  x1,
  input  x2,
  input  x3,
  output y
);

  wire A_out, B_out, C_out, D_out;

  and A (A_out, x0, x1);
  and B (B_out, x2, ~x3);  // AND_Gate
  and C (C_out, x0, x2);
  and D (D_out, x1, ~x2, x3);  // AND_Gate
  or or_1 (y, A_out, B_out, C_out, D_out);

  // Notes on the sheet:
  //   Task1 y-=sum (3,4,5,6,7,10,11,13,15)
endmodule

module TaskTwo (
  input  x0,
  input  x1,
  input  x2,
  input  x3,
  output y
);

  wire A_out, B_out;

  and A (A_out, x0, x2);
  and B (B_out, ~x0, ~x2);  // AND_Gate
  or or_1 (y, A_out, B_out);

  // Notes on the sheet:
  //   y=sum(0,2,5,7,8,10,13,15)
endmodule

module TaskThree (
  input  x0,
  input  x1,
  input  x2,
  input  x3,
  output y
);

  wire A_out, B_out, C_out, D_out;

  and A (A_out, ~x0, ~x1, x2, ~x3);  // AND_Gate
  and B (B_out, x0, ~x1, ~x1, ~x2);  // AND_Gate
  and C (C_out, x1, x2, ~x3);  // AND_Gate
  and D (D_out, ~x0, x1, ~x3);  // AND_Gate
  or or_1 (y, A_out, B_out, C_out, D_out);
endmodule
